# Fritzing sketch electronic_sketch (saved by Fritzing 1.0.4)
breadboards: 1

parts:
  Composant1 = Arduino Uno (Rev3) - ICSP  # not connected
  LCD1 = LCD screen  # not connected
  IC1 = SELECTOR_MULTIPLEXER [package=so016]  # not connected
  M3 = RioRand LM2596
  Composant2 = InvenSense MPU6050  # not connected
  M5 = Stepper Motor - Bipolar
  RE1 = Rotary Encoder [package=THT]  # not connected
  Arduino_CNC_Shield_V3_00_1 = Arduino_CNC_V3.00
  Power_plug2 = Power plug
  JL012-13-5_1 = JL012-13-5.2 Lever (Limit) Switch SPDT + NO + NC [part_number=JL012-13-5.2]
  JL012-13-5_2 = JL012-13-5.2 Lever (Limit) Switch SPDT + NO + NC [part_number=JL012-13-5.2]
  J1 = Basic Servo
  M8 = Dagu DGServo 9g (Top view) [part_number=RS001B]
  Composant3 = Arduino Uno (Rev3) - ICSP
  M9 = Dagu DGServo 9g (Top view) [part_number=RS001B]

nets:
  N1: M3.Pin_1, Arduino_CNC_Shield_V3_00_1.POWER_+, Power_plug2.VCC
  N2: M3.Pin_2, Arduino_CNC_Shield_V3_00_1.POWER_-, Power_plug2.GND
  VCC: M3.Pin_3, J1.vcc, M8.vcc, Composant3.VIN, M9.vcc
  GND: M3.Pin_4, J1.gnd, M8.gnd, Composant3.GND, M9.gnd
  N3: M5.A, Arduino_CNC_Shield_V3_00_1.Z-MTR_'4'
  N4: M5.C, Arduino_CNC_Shield_V3_00_1.Z-MTR_'3'
  N5: M5.B, Arduino_CNC_Shield_V3_00_1.Z-MTR_'2'
  N6: M5.D, Arduino_CNC_Shield_V3_00_1.Z-MTR_'1'
  N7: Arduino_CNC_Shield_V3_00_1.RX, Composant3.D0/RX
  N8: Arduino_CNC_Shield_V3_00_1.TX, Composant3.D1/TX
  N9: Arduino_CNC_Shield_V3_00_1.End_Stops_Y+_(and_Y-), JL012-13-5_1.C
  N10: Arduino_CNC_Shield_V3_00_1.End_Stops_Y+_(Gnd), JL012-13-5_1.NC
  N11: Arduino_CNC_Shield_V3_00_1.End_Stops_X+_(and_X-), JL012-13-5_2.C
  N12: Arduino_CNC_Shield_V3_00_1.End_Stops_X+_(Gnd), JL012-13-5_2.NC
  N13: J1.pulse, Composant3.D11_PWM/MOSI
  N14: M8.pulse, Composant3.D9_PWM
  N15: Composant3.D10_PWM/SS, M9.pulse

custom parts:
  Arduino_CNC_V3.00: Protoneer Arduino CNC Shield V3.00 If using Grbl V0.9: The “A” axis can not be used (yet). The “SCL” (Arduino A5) pin is now used for 'Probing' input. The “End Stops Z+ & Z-” (Arduino D11) and “SpnEn” (Arduino D12) have been switched!
  JL012-13-5.2 Lever (Limit) Switch SPDT + NO + NC: Micro Switch; Model No.: JL012-13.5-2; Actuator Action: Momentary; Actuator Type: Hinge Lever; Contact Configuration: 1NO, 1NC (SPDT) Temperature -25~65℃；Relative humidity: below 85%; Rate Voltage: 125V AC; Rated Current: 1A.
